// Logisim project s-mips.circ as structural Verilog: 22 circuits, main circuit S-MIPS Board
module S_MIPS_Board (
  input  DESHABILITAR_DISPATCHER,
  output halt
);

  wire button_1_out, CLK, CS, d_ff_1_q, LCLR, LoadRAM, LoadRAMOn, LW, R_R_W, R_W, ram_dispatcher_1_finished,
       RCS, Reset_out, RST, TTY_EN;
  wire [2:0] KDB;
  wire [3:0] LMask, Mask, ram_1_read_time, ram_1_write_time, RMask;
  wire [6:0] KDB_DATA, TTY_DATA;
  wire [15:0] Addr, LAddr, RAddr;
  wire [31:0] I0, I1, I2, I3, LData, ram_1_data_out_0, ram_1_data_out_1, ram_1_data_out_2, ram_1_data_out_3,
       RI0, RI1, RI2, RI3;

  TTY #(.rows(25), .cols(80)) tty_1 (.data(TTY_DATA), .clk(CLK), .we(TTY_EN), .clr(RST));
  not not_1 (LoadRAMOn, ram_dispatcher_1_finished);
  RAM_Dispatcher ram_dispatcher_1 (
    .WriteTime(ram_1_write_time), .Clock(CLK), .Data(LData), .Address(LAddr), .Mask(LMask),
    .Finished(ram_dispatcher_1_finished), .Write(LW), .CLR(LCLR));
  Keyboard #(.buflen(64)) keyboard_1 (.clk(CLK), .re(KDB[0]), .avail(KDB[2]), .data(KDB_DATA));  // open: clr
  RAM ram_1 (
    .Address(RAddr), .Data_Out_0(ram_1_data_out_0), .Data_Out_1(ram_1_data_out_1),
    .Data_Out_2(ram_1_data_out_2), .Data_Out_3(ram_1_data_out_3), .Data_In_0(RI0), .Data_In_1(RI1),
    .Data_In_2(RI2), .Data_In_3(RI3), .Mask(RMask), .nRead_Write(R_R_W), .Chip_Select(RCS),
    .Read_Time(ram_1_read_time), .Reset(button_1_out), .Write_Time(ram_1_write_time));
  Button button_1 (.out(button_1_out));
  D_Flip_Flop d_ff_1 (.clk(CLK), .D(1'b1), .Q(d_ff_1_q), .reset(Reset_out));  // open: Qn, preset, en
  Button Reset (.out(Reset_out));
  S_MIPS s_mips_1 (
    .Kbd_Enable(KDB[0]), .Address(Addr), .Kbd_Clear(KDB[1]), .Kbd_Available(KDB[2]), .RAM_In_0(I0),
    .Kbd_ASCII_Data(KDB_DATA), .RAM_In_1(I1), .TTY_Enable(TTY_EN), .RAM_In_2(I2), .RAM_In_3(I3),
    .TTY_ASCII_Data(TTY_DATA), .Reset(RST), .RAM_Out_0(ram_1_data_out_0), .Clock(CLK),
    .RAM_Out_1(ram_1_data_out_1), .Stop(halt), .RAM_Out_2(ram_1_data_out_2), .RAM_Out_3(ram_1_data_out_3),
    .Mask(Mask), .Read_Time(ram_1_read_time), .Write_Time(ram_1_write_time), .nRead_Write(R_W),
    .Chip_Select(CS));
  D_Flip_Flop d_ff_2 (.clk(CLK), .D(d_ff_1_q), .Qn(LCLR), .reset(Reset_out));  // open: Q, preset, en
  or or_1 (RST, LCLR, LoadRAM);
  Clock clock_1 (.out(CLK));
  Multiplexer #(.width(32), .enable("false")) multiplexer_1 (.in0(I0), .in1(LData), .out(RI0), .sel(LoadRAM));
  Multiplexer #(.width(32), .enable("false")) multiplexer_2 (.in0(I1), .in1(LData), .out(RI1), .sel(LoadRAM));
  Multiplexer #(.width(32), .enable("false")) multiplexer_3 (.in0(I2), .in1(LData), .out(RI2), .sel(LoadRAM));
  Multiplexer #(.width(32), .enable("false")) multiplexer_4 (.in0(I3), .in1(LData), .out(RI3), .sel(LoadRAM));
  and and_1 (LoadRAM, ~DESHABILITAR_DISPATCHER, LoadRAMOn);  // AND_Gate
  Multiplexer #(.width(16), .enable("false")) multiplexer_5 (.in0(Addr), .in1(LAddr), .out(RAddr), .sel(LoadRAM));
  Multiplexer #(.width(4), .enable("false")) multiplexer_6 (.in0(Mask), .in1(LMask), .out(RMask), .sel(LoadRAM));
  Multiplexer #(.enable("false")) multiplexer_7 (.in0(CS), .in1(LW), .out(RCS), .sel(LoadRAM));
  Multiplexer #(.enable("false")) multiplexer_8 (.in0(R_W), .in1(LW), .out(R_R_W), .sel(LoadRAM));

  // Notes on the sheet:
  //   NO MODIFICAR
  //   Keyboard
endmodule

module RAM (
  input  [15:0] Address,
  input  [31:0] Data_In_0,
  input  [31:0] Data_In_1,
  input  [31:0] Data_In_2,
  input  [31:0] Data_In_3,
  input  [3:0] Mask,
  input  nRead_Write,
  input  Chip_Select,
  input  Reset,
  output [31:0] Data_Out_0,
  output [31:0] Data_Out_1,
  output [31:0] Data_Out_2,
  output [31:0] Data_Out_3,
  output [3:0] Read_Time,
  output [3:0] Write_Time
);

  wire and_2_out, and_3_out, and_4_out, and_5_out, and_6_out, and_7_out, and_8_out, and_9_out, Changed, CLK,
       comparator_2_eq, comparator_3_eq, comparator_4_eq, comparator_5_eq, comparator_6_eq, Count,
       demultiplexer_3_out0, Idle, Idle_q, Load, Load0, Load1, nand_1_out, or_1_out, or_2_out, or_3_out,
       or_4_out, or_5_out, or_6_out, or_7_out, or_8_out, or_9_out, or_10_out, Proc_q, Update_Mem, Zero_Time;
  wire [3:0] counter_1_q, multiplexer_1_out, subtractor_1_out;
  wire [31:0] register_1_q, register_2_q, register_3_q, register_4_q, register_5_q;

  // Probe on 4'b0011
  // Probe on 4'b0010
  Multiplexer #(.width(4), .enable("false")) multiplexer_1 (
    .in0(4'b0011), .in1(4'b0010), .out(multiplexer_1_out), .sel(nRead_Write));
  or or_1 (or_1_out, Idle, Update_Mem);
  or or_2 (or_2_out, ~Chip_Select, Reset);  // OR_Gate
  Subtractor #(.width(4)) subtractor_1 (.a(multiplexer_1_out), .b(4'b0010), .out(subtractor_1_out));  // open: bin, bout
  Demultiplexer #(.enable("false")) demultiplexer_1 (.out0(Idle), .out1(Load0), .in(Idle_q), .sel(Changed));
  D_Flip_Flop u_Idle (.clk(CLK), .D(or_1_out), .Q(Idle_q), .preset(or_2_out));  // open: Qn, en, reset
  // Probe on counter_1_q
  Counter #(.width(4), .max('hf)) counter_1 (
    .load(Load), .D(subtractor_1_out), .count(Count), .Q(counter_1_q), .clk(CLK), .clr(or_3_out));  // open: carry
  or or_3 (or_3_out, ~Chip_Select, Reset);  // OR_Gate
  Comparator_part #(.width(4), .mode("unsigned")) comparator_1 (
    .a(4'b0000), .b(counter_1_q), .eq(Zero_Time));  // open: gt, lt
  or or_4 (or_4_out, Count, Load0, Load1);
  Register #(.width(32)) register_1 (.D(Data_In_0), .en(Chip_Select), .Q(register_1_q), .clk(CLK), .clr(or_5_out));
  or or_5 (or_5_out, ~Chip_Select, Reset);  // OR_Gate
  Register #(.width(32)) register_2 (.D(Data_In_1), .en(Chip_Select), .Q(register_2_q), .clk(CLK), .clr(or_6_out));
  or or_6 (or_6_out, ~Chip_Select, Reset);  // OR_Gate
  Register #(.width(32)) register_3 (.D(Data_In_2), .en(Chip_Select), .Q(register_3_q), .clk(CLK), .clr(or_7_out));
  or or_7 (or_7_out, ~Chip_Select, Reset);  // OR_Gate
  Register #(.width(32)) register_4 (.D(Data_In_3), .en(Chip_Select), .Q(register_4_q), .clk(CLK), .clr(or_8_out));
  or or_8 (or_8_out, ~Chip_Select, Reset);  // OR_Gate
  Register #(.width(32)) register_5 (
    .D({{11{1'b1}}, nRead_Write, Mask, Address}), .en(Chip_Select), .Q(register_5_q), .clk(CLK),
    .clr(or_9_out));
  or or_9 (or_9_out, ~Chip_Select, Reset);  // OR_Gate
  D_Flip_Flop Proc (.clk(CLK), .D(or_4_out), .Q(Proc_q), .reset(or_10_out));  // open: Qn, preset, en
  or or_10 (or_10_out, ~Chip_Select, Reset);  // OR_Gate
  Demultiplexer #(.enable("false")) demultiplexer_2 (
    .out0(Count), .out1(Update_Mem), .in(demultiplexer_3_out0), .sel(Zero_Time));
  Demultiplexer #(.enable("false")) demultiplexer_3 (
    .out0(demultiplexer_3_out0), .out1(Load1), .in(Proc_q), .sel(Changed));
  Clock clock_1 (.out(CLK));
  Comparator_part #(.width(32)) comparator_2 (.a(register_1_q), .b(Data_In_0), .eq(comparator_2_eq));  // open: gt, lt
  Comparator_part #(.width(32)) comparator_3 (.a(register_2_q), .b(Data_In_1), .eq(comparator_3_eq));  // open: gt, lt
  Comparator_part #(.width(32)) comparator_4 (.a(register_3_q), .b(Data_In_2), .eq(comparator_4_eq));  // open: gt, lt
  Comparator_part #(.width(32)) comparator_5 (.a(register_4_q), .b(Data_In_3), .eq(comparator_5_eq));  // open: gt, lt
  Comparator_part #(.width(32)) comparator_6 (
    .a(register_5_q), .b({{11{1'b1}}, nRead_Write, Mask, Address}), .eq(comparator_6_eq));  // open: gt, lt
  nand nand_1 (nand_1_out, comparator_6_eq, comparator_2_eq, comparator_3_eq, comparator_4_eq, comparator_5_eq);
  and and_1 (Changed, nand_1_out, Chip_Select);
  or or_11 (Load, Count, Load1, Load0);
  and and_2 (and_2_out, Mask[0], Update_Mem, nRead_Write);
  and and_3 (and_3_out, Mask[1], Update_Mem, nRead_Write);
  and and_4 (and_4_out, Mask[2], Update_Mem, nRead_Write);
  and and_5 (and_5_out, Mask[3], Update_Mem, nRead_Write);
  RAM_part #(.addrWidth(16), .dataWidth(32), .bus("separate")) ram_1 (
    .addr(Address), .din(Data_In_0), .data(Data_Out_0), .str(and_2_out), .sel(Chip_Select), .clk(CLK),
    .ld(and_6_out), .clr(Reset));
  and and_6 (and_6_out, ~nRead_Write, Idle);  // AND_Gate
  RAM_part #(.addrWidth(16), .dataWidth(32), .bus("separate")) ram_2 (
    .addr(Address), .din(Data_In_1), .data(Data_Out_1), .str(and_3_out), .sel(Chip_Select), .clk(CLK),
    .ld(and_7_out), .clr(Reset));
  and and_7 (and_7_out, ~nRead_Write, Idle);  // AND_Gate
  RAM_part #(.addrWidth(16), .dataWidth(32), .bus("separate")) ram_3 (
    .addr(Address), .din(Data_In_2), .data(Data_Out_2), .str(and_4_out), .sel(Chip_Select), .clk(CLK),
    .ld(and_8_out), .clr(Reset));
  and and_8 (and_8_out, ~nRead_Write, Idle);  // AND_Gate
  RAM_part #(.addrWidth(16), .dataWidth(32), .bus("separate")) ram_4 (
    .addr(Address), .din(Data_In_3), .data(Data_Out_3), .str(and_5_out), .sel(Chip_Select), .clk(CLK),
    .ld(and_9_out), .clr(Reset));
  and and_9 (and_9_out, ~nRead_Write, Idle);  // AND_Gate

  assign Read_Time = 4'b0011;
  assign Write_Time = 4'b0010;

  // Other names for the same wires on the sheet: M0 = Mask[0]; M1 = Mask[1]; M2 = Mask[2]; M3 = Mask[3];
  //   RW = nRead_Write; CLR = Reset; CS = Chip_Select; Load2 = Count

  // Notes on the sheet:
  //   NO MODIFICAR
  //   excepto quizás los valores RT y WT
  //   BANK0
  //   BANK1
  //   BANK2
  //   BANK3
endmodule

module S_MIPS (
  input  Kbd_Available,
  input  [6:0] Kbd_ASCII_Data,
  input  [31:0] RAM_Out_0,
  input  [31:0] RAM_Out_1,
  input  Reset,
  input  [31:0] RAM_Out_2,
  input  Clock,
  input  [31:0] RAM_Out_3,
  input  [3:0] Read_Time,
  input  [3:0] Write_Time,
  output Kbd_Enable,
  output [15:0] Address,
  output Kbd_Clear,
  output TTY_Enable,
  output [6:0] TTY_ASCII_Data,
  output Stop,
  output [31:0] RAM_In_0,
  output [31:0] RAM_In_1,
  output [31:0] RAM_In_2,
  output [31:0] RAM_In_3,
  output [3:0] Mask,
  output nRead_Write,
  output Chip_Select
);

  wire ALU_I, enIC, enPC, enRF, get_data, get_Inst, jmp_I, next_Inst, or_1_out, read_I, ready_data,
       ready_Inst, ready_write, save_I, start, tty, write, write_I;
  wire [31:0] address_t, Inst, multiplexer_1_out, multiplexer_2_out, multiplexer_3_out, multiplexer_4_out,
       raminteraction_1_output, raminteraction_1_output_2, raminteraction_1_output_3,
       raminteraction_1_output_4;

  Multiplexer #(.width(32), .enable("false")) multiplexer_1 (
    .in0(RAM_Out_2), .in1(RAM_In_0), .out(multiplexer_1_out), .sel(write));
  Multiplexer #(.width(32), .enable("false")) multiplexer_2 (
    .in0(RAM_Out_3), .in1(RAM_In_0), .out(multiplexer_2_out), .sel(write));
  Multiplexer #(.width(32), .enable("false")) multiplexer_3 (
    .in0(RAM_Out_0), .in1(RAM_In_0), .out(multiplexer_3_out), .sel(write));
  Multiplexer #(.width(32), .enable("false")) multiplexer_4 (
    .in0(RAM_Out_1), .in1(RAM_In_0), .out(multiplexer_4_out), .sel(write));
  ControlUnit controlunit_1 (
    .in_1(start), .in_2(Clock), .in_3(Reset), .in_4(ready_write), .in_5(ready_data), .in_6(ready_Inst),
    .in_7(ALU_I), .in_8(jmp_I), .in_9(read_I), .in_10(write_I), .in_11(save_I), .in_12(tty),
    .Output(get_Inst), .Output_2(enIC), .Output_3(enPC), .Output_4(enRF), .Output_5(get_data),
    .Output_6(write), .Output_7(Stop), .Output_8(Kbd_Enable), .Output_9(TTY_Enable));
  RamInteraction raminteraction_1 (
    .in_1(multiplexer_3_out), .in_2(multiplexer_4_out), .in_3(multiplexer_1_out), .in_4(multiplexer_2_out),
    .in_5(address_t), .in_6(Read_Time), .in_7(Write_Time), .in_8(Clock), .in_9(Reset), .in_10(get_Inst),
    .in_11(write), .in_12(get_data), .in_13(enIC), .Output(raminteraction_1_output),
    .Output_2(raminteraction_1_output_2), .Output_3(raminteraction_1_output_3),
    .Output_4(raminteraction_1_output_4), .Output_5(Address), .Output_6(Mask), .Output_7(nRead_Write),
    .Output_8(Chip_Select), .Output_9(ready_Inst), .Output_10(ready_data), .Output_11(ready_write));
  Multiplexer #(.select(2), .width(32), .enable("false")) multiplexer_5 (
    .in0(raminteraction_1_output), .in1(raminteraction_1_output_2), .in2(raminteraction_1_output_3),
    .in3(raminteraction_1_output_4), .out(Inst), .sel(address_t[3:2]));
  D_Flip_Flop #(.trigger("falling")) d_ff_1 (
    .clk(Clock), .D(get_Inst), .Q(next_Inst), .en(or_1_out));  // open: Qn, preset, reset
  or or_1 (or_1_out, get_Inst, ready_Inst);
  D_Flip_Flop #(.trigger("falling")) d_ff_2 (.clk(Clock), .D(Reset), .Q(start));  // open: Qn, preset, en, reset
  DataPath datapath_1 (
    .in_1(Clock), .in_2(enRF), .in_3(Inst), .in_4(Reset), .in_5(enPC), .in_6(enIC), .in_7(Kbd_Available),
    .Output_9(TTY_ASCII_Data), .in_9(Kbd_ASCII_Data), .in_8(next_Inst), .Output(ALU_I), .Output_2(read_I),
    .Output_3(write_I), .Output_4(address_t), .Output_5(RAM_In_0), .Output_6(jmp_I), .Output_7(save_I),
    .Output_8(tty));

  assign Kbd_Clear = Reset;
  assign RAM_In_1 = RAM_In_0;
  assign RAM_In_2 = RAM_In_0;
  assign RAM_In_3 = RAM_In_0;

  // Other names for the same wires on the sheet: selector[1:0] = address_t[3:2]; CLK = Clock; CS = Chip_Select;
  //   KBD_AVAIL = Kbd_Available; CLR = Reset; KBD_CLR = Reset; KBD_DATA[6:0] = Kbd_ASCII_Data; R_Out[31:0] = RAM_In_0;
  //   RAM_INPUT_0[31:0] = RAM_In_0; RAM_INPUT_1[31:0] = RAM_In_0; RAM_INPUT_2[31:0] = RAM_In_0;
  //   RAM_INPUT_3[31:0] = RAM_In_0; RAM_A[15:0] = Address; RAM_MASK[3:0] = Mask; RAM_OUTPUT_0[31:0] = RAM_Out_0;
  //   RAM_OUTPUT_1[31:0] = RAM_Out_1; RAM_OUTPUT_2[31:0] = RAM_Out_2; RAM_OUTPUT_3[31:0] = RAM_Out_3;
  //   RW = nRead_Write; TTY_DATA[6:0] = TTY_ASCII_Data

  // Notes on the sheet:
  //   RAM ADDRESS
  //   DATA FROM RAM
  //   DATA TO RAM
  //   DATA WRITE MASK
  //   RAM TIMING
  //   RAM CONTROL
  //   KEYBOARD
  //   TTY
  //   SEQUENCING
endmodule

module RAM_Dispatcher (
  input  [3:0] WriteTime,
  input  Clock,
  input  CLR,
  output [31:0] Data,
  output [15:0] Address,
  output [3:0] Mask,
  output Finished,
  output Write
);

  wire demultiplexer_2_out1, demultiplexer_3_out1, End, IDLE_q, IncAddr, Load, or_1_out, or_2_out, While_q,
       WriteEnd;
  wire [3:0] counter_1_q;
  wire [31:0] CurrentAddress_q;

  Counter #(.width(32), .max('hffffffff)) CurrentAddress (
    .count(IncAddr), .Q({CurrentAddress_q[31:18], Address, CurrentAddress_q[1:0]}), .clk(Clock), .clr(CLR));  // open: load, D, carry
  or or_1 (or_1_out, IncAddr, demultiplexer_3_out1, Finished);
  D_Flip_Flop IDLE (.clk(Clock), .D(or_1_out), .Q(IDLE_q), .preset(CLR));  // open: Qn, en, reset
  Demultiplexer #(.enable("false")) demultiplexer_1 (.out0(Load), .out1(Finished), .in(IDLE_q), .sel(End));
  D_Flip_Flop While (.clk(Clock), .D(or_2_out), .Q(While_q), .reset(CLR));  // open: Qn, preset, en
  or or_2 (or_2_out, Write, Load);
  RAM_part #(.addrWidth(18), .dataWidth(32)) ram_1 (
    .addr({Address, CurrentAddress_q[1:0]}), .data(Data), .clk(Clock));  // open: sel, ld, clr
  Demultiplexer #(.enable("false")) demultiplexer_2 (
    .out0(Write), .out1(demultiplexer_2_out1), .in(While_q), .sel(WriteEnd));
  Decoder #(.select(2)) decoder_1 (
    .out0(Mask[0]), .out1(Mask[1]), .out2(Mask[2]), .out3(Mask[3]), .sel(CurrentAddress_q[1:0]));  // open: en
  Demultiplexer #(.enable("false")) demultiplexer_3 (
    .out0(IncAddr), .out1(demultiplexer_3_out1), .in(demultiplexer_2_out1), .sel(End));
  Counter #(.width(4), .max('hf)) counter_1 (
    .load(Load), .D(WriteTime), .count(Write), .Q(counter_1_q), .clk(Clock));  // open: carry, clr
  Comparator_part #(.width(32)) comparator_1 (.a(Data), .b({32{1'b1}}), .eq(End));  // open: gt, lt
  Comparator_part #(.width(4)) comparator_2 (.a(4'b0000), .b(counter_1_q), .eq(WriteEnd));  // open: gt, lt

  // Other names for the same wires on the sheet: CLK = Clock; Count = Write; WT[3:0] = WriteTime
endmodule

module InstructionDecoder (
  input  [31:0] in_1,
  output [4:0] Output,
  output [5:0] Output_2,
  output [25:0] Output_3,
  output [4:0] Output_4,
  output [15:0] Output_5,
  output [4:0] Output_6,
  output Output_7,
  output Output_8,
  output Output_9,
  output Output_10,
  output Output_11,
  output Output_12,
  output Output_13,
  output Output_14,
  output Output_15,
  output Output_16,
  output Output_17,
  output Output_18,
  output Output_19,
  output Output_20,
  output Output_21,
  output Output_22,
  output Output_23,
  output Output_24,
  output Output_25,
  output Output_26,
  output Output_27,
  output Output_28,
  output Output_29,
  output Output_30,
  output Output_31,
  output Output_32,
  output Output_33,
  output Output_34,
  output Output_35,
  output Output_36,
  output Output_37,
  output Output_38,
  output Output_39,
  output Output_40,
  output Output_41,
  output Output_42,
  output Output_43,
  output Output_44,
  output Output_45,
  output Output_46,
  output Output_47
);

  wire _000000, _111111, ADD, AND, comparator_16_eq, comparator_17_eq, comparator_18_eq, comparator_19_eq,
       comparator_20_eq, comparator_21_eq, comparator_22_eq, comparator_23_eq, comparator_24_eq,
       comparator_25_eq, comparator_26_eq, comparator_27_eq, comparator_28_eq, comparator_29_eq,
       comparator_30_eq, comparator_31_eq, comparator_32_eq, comparator_33_eq, comparator_34_eq,
       comparator_35_eq, comparator_36_eq, comparator_37_eq, comparator_38_eq, comparator_39_eq, DIV, MUL,
       OR, SLT, SLTI, XOR;

  Comparator_part #(.width(6)) comparator_1 (.a(in_1[31:26]), .b(6'b001000), .eq(Output_21));  // open: gt, lt
  Comparator_part #(.width(6)) comparator_2 (.a(in_1[31:26]), .b(6'b010010), .eq(Output_31));  // open: gt, lt
  Comparator_part #(.width(6)) comparator_3 (.a(in_1[31:26]), .b(6'b001010), .eq(Output_23));  // open: gt, lt
  Comparator_part #(.width(6)) comparator_4 (.a(in_1[31:26]), .b(6'b010001), .eq(Output_27));  // open: gt, lt
  Comparator_part #(.width(6)) comparator_5 (.a(in_1[31:26]), .b(6'b000100), .eq(Output_24));  // open: gt, lt
  Comparator_part #(.width(6)) comparator_6 (.a(in_1[31:26]), .b(6'b000101), .eq(Output_28));  // open: gt, lt
  Comparator_part #(.width(6)) comparator_7 (.a(in_1[31:26]), .b(6'b000110), .eq(Output_32));  // open: gt, lt
  Comparator_part #(.width(6)) comparator_8 (.a(in_1[31:26]), .b(6'b000111), .eq(Output_36));  // open: gt, lt
  Comparator_part #(.width(6)) comparator_9 (.a(in_1[31:26]), .b(6'b000001), .eq(Output_40));  // open: gt, lt
  or or_1 (MUL, Output_14, Output_16);
  or or_2 (DIV, Output_18, Output_20);
  or or_3 (SLT, Output_8, Output_10);
  or or_4 (SLTI, Output_23, Output_27);
  Comparator_part #(.width(6)) comparator_10 (.a(in_1[31:26]), .b(6'b100011), .eq(Output_42));  // open: gt, lt
  Comparator_part #(.width(6)) comparator_11 (.a(in_1[31:26]), .b(6'b101011), .eq(Output_22));  // open: gt, lt
  Comparator_part #(.width(6)) comparator_12 (.a(in_1[31:26]), .b(6'b001101), .eq(Output_35));  // open: gt, lt
  Comparator_part #(.width(6)) comparator_13 (.a(in_1[31:26]), .b(6'b001110), .eq(Output_39));  // open: gt, lt
  or or_5 (AND, Output_12, Output_31);
  or or_6 (OR, Output_15, Output_35);
  or or_7 (XOR, Output_19, Output_39);
  or or_8 (ADD, Output_9, Output_21);
  Comparator_part #(.width(6)) comparator_14 (.a(in_1[31:26]), .b({6{1'b0}}), .eq(_000000));  // open: gt, lt
  Comparator_part #(.width(6)) comparator_15 (.a(in_1[31:26]), .b({6{1'b1}}), .eq(_111111));  // open: gt, lt
  Comparator_part #(.width(6)) comparator_16 (.a(in_1[5:0]), .b({6{1'b1}}), .eq(comparator_16_eq));  // open: gt, lt
  Comparator_part #(.width(6)) comparator_17 (.a(in_1[5:0]), .b(6'b000001), .eq(comparator_17_eq));  // open: gt, lt
  Comparator_part #(.width(6)) comparator_18 (.a(in_1[5:0]), .b(6'b000010), .eq(comparator_18_eq));  // open: gt, lt
  Comparator_part #(.width(6)) comparator_19 (.a(in_1[5:0]), .b(6'b000100), .eq(comparator_19_eq));  // open: gt, lt
  and and_1 (Output_26, _111111, comparator_16_eq);
  and and_2 (Output_30, _111111, comparator_17_eq);
  and and_3 (Output_34, _111111, comparator_18_eq);
  and and_4 (Output_38, _111111, comparator_19_eq);
  or or_9 (Output_43, MUL, DIV, SLT, SLTI, AND, OR, XOR, ADD, Output_17, Output_11);
  Comparator_part #(.width(6)) comparator_20 (.a(in_1[31:26]), .b(6'b111000), .eq(comparator_20_eq));  // open: gt, lt
  Comparator_part #(.width(6)) comparator_21 (.a(in_1[5:0]), .b({6{1'b0}}), .eq(comparator_21_eq));  // open: gt, lt
  Comparator_part #(.width(6)) comparator_22 (.a(in_1[31:26]), .b(6'b111000), .eq(comparator_22_eq));  // open: gt, lt
  Comparator_part #(.width(6)) comparator_23 (.a(in_1[5:0]), .b(6'b000001), .eq(comparator_23_eq));  // open: gt, lt
  and and_5 (Output_7, _000000, comparator_24_eq);
  Comparator_part #(.width(6)) comparator_24 (.a(in_1[5:0]), .b({6{1'b0}}), .eq(comparator_24_eq));  // open: gt, lt
  and and_6 (Output_9, _000000, comparator_25_eq);
  Comparator_part #(.width(6)) comparator_25 (.a(in_1[5:0]), .b(6'b100000), .eq(comparator_25_eq));  // open: gt, lt
  and and_7 (Output_11, _000000, comparator_26_eq);
  Comparator_part #(.width(6)) comparator_26 (.a(in_1[5:0]), .b(6'b100010), .eq(comparator_26_eq));  // open: gt, lt
  and and_8 (Output_14, _000000, comparator_27_eq);
  Comparator_part #(.width(6)) comparator_27 (.a(in_1[5:0]), .b(6'b011000), .eq(comparator_27_eq));  // open: gt, lt
  and and_9 (Output_16, _000000, comparator_28_eq);
  Comparator_part #(.width(6)) comparator_28 (.a(in_1[5:0]), .b(6'b011001), .eq(comparator_28_eq));  // open: gt, lt
  and and_10 (Output_18, _000000, comparator_29_eq);
  Comparator_part #(.width(6)) comparator_29 (.a(in_1[5:0]), .b(6'b011010), .eq(comparator_29_eq));  // open: gt, lt
  and and_11 (Output_20, _000000, comparator_30_eq);
  Comparator_part #(.width(6)) comparator_30 (.a(in_1[5:0]), .b(6'b011011), .eq(comparator_30_eq));  // open: gt, lt
  and and_12 (Output_8, _000000, comparator_31_eq);
  Comparator_part #(.width(6)) comparator_31 (.a(in_1[5:0]), .b(6'b101010), .eq(comparator_31_eq));  // open: gt, lt
  and and_13 (Output_25, comparator_20_eq, comparator_21_eq);
  and and_14 (Output_29, comparator_22_eq, comparator_23_eq);
  or or_10 (Output_44, Output_24, Output_40, Output_28, Output_36, Output_32, Output_13, Output_33, Output_7);
  or or_11 (Output_45, Output_22, Output_29);
  Comparator_part #(.width(6)) comparator_32 (.a(in_1[5:0]), .b(6'b101011), .eq(comparator_32_eq));  // open: gt, lt
  Comparator_part #(.width(6)) comparator_33 (.a(in_1[5:0]), .b(6'b100100), .eq(comparator_33_eq));  // open: gt, lt
  Comparator_part #(.width(6)) comparator_34 (.a(in_1[5:0]), .b(6'b100101), .eq(comparator_34_eq));  // open: gt, lt
  Comparator_part #(.width(6)) comparator_35 (.a(in_1[5:0]), .b(6'b100111), .eq(comparator_35_eq));  // open: gt, lt
  Comparator_part #(.width(6)) comparator_36 (.a(in_1[5:0]), .b(6'b101000), .eq(comparator_36_eq));  // open: gt, lt
  Comparator_part #(.width(6)) comparator_37 (.a(in_1[5:0]), .b(6'b001000), .eq(comparator_37_eq));  // open: gt, lt
  Comparator_part #(.width(6)) comparator_38 (.a(in_1[5:0]), .b(6'b010000), .eq(comparator_38_eq));  // open: gt, lt
  Comparator_part #(.width(6)) comparator_39 (.a(in_1[5:0]), .b(6'b010010), .eq(comparator_39_eq));  // open: gt, lt
  or or_12 (Output_47, Output_34, Output_41, Output_38, Output_37, Output_30);
  or or_13 (Output_46, Output_42, Output_25);
  and and_15 (Output_10, _000000, comparator_32_eq);
  and and_16 (Output_12, _000000, comparator_33_eq);
  and and_17 (Output_15, _000000, comparator_34_eq);
  and and_18 (Output_17, _000000, comparator_35_eq);
  and and_19 (Output_19, _000000, comparator_36_eq);
  and and_20 (Output_33, _000000, comparator_37_eq);
  and and_21 (Output_37, _000000, comparator_38_eq);
  and and_22 (Output_41, _000000, comparator_39_eq);
  Comparator_part #(.width(6)) comparator_40 (.a(in_1[31:26]), .b(6'b000010), .eq(Output_13));  // open: gt, lt

  assign Output = in_1[25:21];
  assign Output_2 = in_1[5:0];
  assign Output_3 = in_1[25:0];
  assign Output_4 = in_1[20:16];
  assign Output_5 = in_1[15:0];
  assign Output_6 = in_1[15:11];

  // Other names for the same wires on the sheet: add_t = Output_9; addi = Output_21; ALU_inst = Output_43;
  //   and_t = Output_12; andi = Output_31; beq = Output_24; bgtz = Output_36; blez = Output_32; bltz = Output_40;
  //   bne = Output_28; div_t = Output_18; divu = Output_20; halt = Output_26; Const[15:0] = in_1[15:0];
  //   FC[5:0] = in_1[5:0]; Salto[25:0] = in_1[25:0]; RD[4:0] = in_1[15:11]; RT[4:0] = in_1[20:16];
  //   RS[4:0] = in_1[25:21]; OpCode[5:0] = in_1[31:26]; j = Output_13; jmp_inst = Output_44; jr = Output_33;
  //   kbd = Output_38; lw = Output_42; mfhi = Output_37; mflo = Output_41; mult = Output_14; mulu = Output_16;
  //   nop = Output_7; nor = Output_17; or_t = Output_15; ori = Output_35; pop = Output_25; push = Output_29;
  //   read_mem_inst = Output_46; rnd = Output_34; save_inst = Output_47; slt_t = Output_8; slti_t = Output_23;
  //   sltiu = Output_27; sltu = Output_10; sub = Output_11; sw = Output_22; tty = Output_30;
  //   write_mem_inst = Output_45; xor_t = Output_19; xori = Output_39

  // Notes on the sheet:
  //   Particionar Instruccion
  //   Instrucciones De Tipo I:
  //   Instrucciones De Tipo R
  //   Instrucciones DeTipo J
endmodule

module AluSelector (
  input  in_1,
  input  in_2,
  input  in_3,
  input  in_4,
  input  in_5,
  input  in_6,
  input  in_7,
  input  in_8,
  input  in_9,
  input  in_10,
  input  in_11,
  input  in_12,
  input  in_13,
  input  in_14,
  input  in_15,
  input  in_16,
  input  in_17,
  input  in_18,
  output [3:0] Output,
  output Output_2,
  output Output_3
);

  wire Add, And, Div, Mult, Or, or_2_out, Slt, Xor;

  or or_1 (Output_2, in_13, in_16, in_17, in_18, or_2_out);
  or or_2 (or_2_out, in_14, in_15);
  or or_3 (Add, in_1, in_13);
  or or_4 (Mult, in_3, in_4);
  or or_5 (Div, in_5, in_6);
  or or_6 (And, in_9, in_16);
  or or_7 (Slt, in_7, in_8, in_14, in_15);
  or or_8 (Or, in_10, in_17);
  or or_9 (Xor, in_12, in_18);
  or or_10 (Output_3, in_4, in_6, in_8, in_15);
  Priority_Encoder #(.select(4)) priority_encoder_1 (
    .in0(1'b1), .in1(in_2), .in2(Mult), .in3(Div), .in4(And), .in5(Or), .in6(in_11), .in7(Xor), .in8(Slt),
    .out(Output));  // open: in9, in10, in11, in12, in13, in14, in15, gs, en_out, en_in

  // Other names for the same wires on the sheet: add_t = in_1; addi = in_13; and_t = in_9; andi = in_16; div_t = in_5;
  //   divu = in_6; I_Op = Output_2; mult_t = in_3; mulu = in_4; nor = in_11; NoSign = Output_3; or_t = in_10;
  //   ori = in_17; slt_t = in_7; slti = in_14; sltiu = in_15; sltu = in_8; sub = in_2; xor_t = in_12; xori = in_18

  // Notes on the sheet:
  //   Operacion Aritmeticas de Tipo I:
  //   Operaciones sin tener en cuenta el Signo:
endmodule

module ProgramCounter (
  input  in_1,
  input  in_2,
  input  in_3,
  input  [31:0] in_4,
  output [31:0] Output
);

  Register #(.width(32)) register_1 (.D(in_4), .en(in_2), .Q(Output), .clk(in_1), .clr(in_3));

  // Other names for the same wires on the sheet: Clk = in_1; enable = in_2; reset = in_3
endmodule

module BranchControl (
  input  [15:0] in_1,
  input  [31:0] InstActual,
  input  [25:0] Salto,
  input  [31:0] RS,
  input  [31:0] RT,
  input  in_6,
  input  in_7,
  input  in_8,
  input  in_9,
  input  in_10,
  input  in_11,
  input  in_12,
  input  in_13,
  output [31:0] Output
);

  wire and_1_out, and_2_out, and_3_out, and_4_out, and_5_out, comparator_1_eq, FC, RS_0, RS__0, RS__RT;
  wire [1:0] selector;
  wire [27:2] jmp;
  wire [31:0] IA_4, IA_4_CN;
  wire [31:18] CN;

  Comparator_part #(.width(32)) comparator_1 (.a({32{1'b0}}), .b(RS), .eq(comparator_1_eq), .lt(RS_0));  // open: gt
  or or_1 (RS__0, comparator_1_eq, RS_0);
  Comparator_part #(.width(32)) comparator_2 (.a(RS), .b(RT), .eq(RS__RT));  // open: gt, lt
  and and_1 (and_1_out, RS__RT, in_6);
  and and_2 (and_2_out, ~RS__RT, in_7);  // AND_Gate
  and and_3 (and_3_out, RS__0, in_8);
  and and_4 (and_4_out, ~RS__0, in_9);  // AND_Gate
  and and_5 (and_5_out, RS_0, in_10);
  or or_2 (FC, and_1_out, and_2_out, and_3_out, and_4_out, and_5_out);
  Adder #(.width(32)) adder_1 (.a(InstActual), .b(32'h4), .out(IA_4));  // open: cin, cout
  assign CN = {{13{in_1[15]}}, in_1[15]};  // Bit_Extender bit_extender_1
  Adder #(.width(32)) adder_2 (.a(IA_4), .b({CN, in_1, 2'b00}), .out(IA_4_CN));  // open: cin, cout
  Multiplexer #(.select(2), .width(32), .enable("false")) multiplexer_1 (
    .in0(IA_4), .in1(IA_4_CN), .in2({InstActual[31:28], jmp, 2'b00}), .in3(RS), .out(Output), .sel(selector));
  Priority_Encoder #(.select(2)) priority_encoder_1 (
    .in0(1'b1), .in1(FC), .in2(in_12), .in3(in_11), .out(selector));  // open: gs, en_out, en_in

  // Other names for the same wires on the sheet: beq = in_6; bgtz = in_9; blez = in_8; bltz = in_10; bne = in_7;
  //   CN[17:2] = in_1; const[15:0] = in_1; IA[31:0] = InstActual; j = in_12; salto_t[25:0] = jmp;
  //   jmp[31:28] = InstActual[31:28]; jr = in_11; nop = in_13
endmodule

module DataPath (
  input  in_1,
  input  in_2,
  input  [31:0] in_3,
  input  in_4,
  input  in_5,
  input  in_6,
  input  in_7,
  input  in_8,
  input  [6:0] in_9,
  output Output,
  output Output_2,
  output Output_3,
  output [31:0] Output_4,
  output [31:0] Output_5,
  output Output_6,
  output Output_7,
  output Output_8,
  output [6:0] Output_9
);

  wire Add, Addi, And, Andi, beq, bgtz, blez, bltz, bne, Div, Divu, halt, I_Op, j, jr, kbd, lw, mfhi, mflo,
       Mult, Mulu, nop, Nor, Or, Ori, pop, push, rnd, sign, Slt, Slti, Sltiu, Sltu, Sub, sw, Xor, Xori;
  wire [3:0] SelALU;
  wire [4:0] multiplexer_3_out, RD, RS, RT;
  wire [5:0] FC;
  wire [15:0] Const;
  wire [25:0] Salto;
  wire [31:0] ALU_Out, HI, instructioncatcher_1_output, LO, multiplexer_1_out, multiplexer_2_out, PC_In,
       PC_Out, random, register_file_input_1_output, RT_t, SP;
  wire [31:7] RS_t;
  wire [31:31] and_1_out;

  Random #(.width(32)) random_1 (.clk(in_1), .next(rnd), .out(random));  // open: clr
  InstructionCatcher instructioncatcher_1 (
    .in_1(in_1), .in_2(in_4), .in_3(in_6), .in_4(in_3), .Output(instructioncatcher_1_output));
  // Probe on RD
  // Probe on RS
  AluSelector aluselector_1 (
    .in_1(Add), .in_2(Sub), .in_3(Mult), .in_4(Mulu), .in_5(Div), .in_6(Divu), .in_7(Slt), .in_8(Sltu),
    .in_9(And), .in_10(Or), .in_11(Nor), .in_12(Xor), .in_13(Addi), .in_14(Slti), .in_15(Sltiu),
    .in_16(Andi), .in_17(Ori), .in_18(Xori), .Output_2(I_Op), .Output_3(sign), .Output(SelALU));
  InstructionDecoder instructiondecoder_1 (
    .Output(RS), .Output_2(FC), .in_1(instructioncatcher_1_output), .Output_3(Salto), .Output_4(RT),
    .Output_5(Const), .Output_6(RD), .Output_7(nop), .Output_8(Slt), .Output_9(Add), .Output_10(Sltu),
    .Output_11(Sub), .Output_12(And), .Output_13(j), .Output_14(Mult), .Output_15(Or), .Output_16(Mulu),
    .Output_17(Nor), .Output_18(Div), .Output_19(Xor), .Output_20(Divu), .Output_21(Addi), .Output_22(sw),
    .Output_23(Slti), .Output_24(beq), .Output_25(pop), .Output_26(halt), .Output_27(Sltiu), .Output_28(bne),
    .Output_29(push), .Output_30(Output_8), .Output_31(Andi), .Output_32(blez), .Output_33(jr),
    .Output_34(rnd), .Output_35(Ori), .Output_36(bgtz), .Output_37(mfhi), .Output_38(kbd), .Output_39(Xori),
    .Output_40(bltz), .Output_41(mflo), .Output_42(lw), .Output_43(Output), .Output_44(Output_6),
    .Output_45(Output_3), .Output_46(Output_2), .Output_47(Output_7));
  // Probe on SelALU
  and and_1 (and_1_out[31], Const[15], ~Ori, ~Andi, ~Xori);  // AND_Gate
  Multiplexer #(.width(32), .enable("false")) multiplexer_1 (
    .in0(RT_t), .in1({{16{and_1_out[31]}}, Const}), .out(multiplexer_1_out), .sel(I_Op));
  ALU alu_1 (
    .sign(sign), .Selector(SelALU), .A({RS_t, Output_9}), .B(multiplexer_1_out), .Output(ALU_Out),
    .Output_2(LO), .Output_3(HI), .in_2(in_1));
  // Probe on SelALU
  // Probe on ALU_Out
  // Probe on in_3
  ProgramCounter programcounter_1 (.in_1(in_1), .in_2(in_5), .in_3(in_4), .in_4(PC_In), .Output(PC_Out));
  Multiplexer #(.width(32), .enable("false")) multiplexer_2 (
    .in0({RS_t, Output_9}), .in1(RT_t), .out(multiplexer_2_out), .sel(sw));
  // Probe on PC_Out
  BranchControl branchcontrol_1 (
    .in_1(Const), .InstActual(PC_Out), .Salto(Salto), .RS({RS_t, Output_9}), .RT(RT_t), .in_6(beq),
    .in_7(bne), .in_8(blez), .in_9(bgtz), .in_10(bltz), .in_11(jr), .in_12(j), .in_13(nop), .Output(PC_In));
  // Probe on RD
  // Probe on multiplexer_3_out
  Register_File_Input register_file_input_1 (
    .in_1(lw), .in_2(mfhi), .in_3(kbd), .in_5(ALU_Out), .in_6(pop), .in_7(mflo), .in_8(rnd), .in_9(random),
    .Kbd_data(in_9), .in_11(in_3), .in_12(HI), .in_13(LO), .Output(register_file_input_1_output), .in_4(in_7));
  // Probe on register_file_input_1_output
  SwapBits swapbits_1 (.in_1(multiplexer_2_out), .Output(Output_5));
  // Probe on PC_In
  Multiplexer #(.width(5), .enable("false")) multiplexer_3 (.in0(RD), .in1(RT), .out(multiplexer_3_out), .sel(I_Op));
  MemoryAddress memoryaddress_1 (
    .in_1(PC_Out), .in_2(ALU_Out), .in_3(SP), .in_4(lw), .in_5(sw), .in_6(pop), .in_7(push), .in_8(in_8),
    .Output(Output_4));
  // Probe on {RS_t, Output_9}
  // Probe on RS
  RegisterFile registerfile_1 (
    .Data(register_file_input_1_output), .Selector_B(RT), .Selector_A(RS), .Data_Adress(multiplexer_3_out),
    .R_W(in_2), .Clk(in_1), .Rst(in_4), .push(push), .pop(pop), .enPC(in_5), .Output({RS_t, Output_9}),
    .Ouput(RT_t), .Output_2(SP));
  // Probe on RT

  // Other names for the same wires on the sheet: Address[31:0] = Output_4; ALU_inst = Output; Clk = in_1;
  //   En_IC = in_6; EnPC = in_5; Instruction[31:0] = in_3; jmp_inst = Output_6; Kbd_Ava = in_7; Kbd_Data[6:0] = in_9;
  //   nexti = in_8; R_W = in_2; read_inst = Output_2; Reset = in_4; RS_t[6:0] = Output_9; tty_data[6:0] = Output_9;
  //   save_inst = Output_7; tty = Output_8; write_inst = Output_3

  // Notes on the sheet:
  //   Inputs:
  //   Otras Operaciones:
  //   Outputs:
endmodule

module InstructionCatcher (
  input  in_1,
  input  in_2,
  input  in_3,
  input  [31:0] in_4,
  output [31:0] Output
);

  wire [31:0] register_1_q;

  Register #(.width(32)) register_1 (.D(in_4), .en(in_3), .Q(register_1_q), .clk(in_1), .clr(in_2));
  SwapBits swapbits_1 (.in_1(register_1_q), .Output(Output));

  // Other names for the same wires on the sheet: clock = in_1; enable = in_3; instruction[31:0] = in_4; reset = in_2
endmodule

module ALU (
  input  sign,
  input  in_2,
  input  [3:0] Selector,
  input  [31:0] A,
  input  [31:0] B,
  output [31:0] Output,
  output [31:0] Output_2,
  output [31:0] Output_3
);

  wire div, enable, mult;
  wire [31:0] add, \and , div_rem, div_res, HI, LO, multiplexer_2_out, multiplexer_3_out, \nand , \nor ,
       \or , slt, sub, \xor ;

  Multiplexer #(.select(4), .width(32)) multiplexer_1 (
    .in0(add), .in1(sub), .in4(\and ), .in5(\or ), .in6(\nor ), .in7(\xor ), .in8(slt), .out(Output),
    .sel(Selector));  // open: in2, in3, in9, in10, in11, in12, in13, in14, in15, en
  Adder #(.width(32)) adder_1 (.a(A), .b(B), .out(add));  // open: cin, cout
  Subtractor #(.width(32)) subtractor_1 (.a(A), .b(B), .out(sub));  // open: bin, bout
  assign \and  = A & B;  // AND_Gate and_1, 32 bits wide
  assign \nand  = ~(A & B);  // NAND_Gate nand_1, 32 bits wide
  assign \nor  = ~(A | B);  // NOR_Gate nor_1, 32 bits wide
  assign \xor  = A ^ B;  // XOR_Gate xor_1, 32 bits wide
  Comparator comparator_1 (.A(A), .B(B), .sign(sign), .\output (slt));
  divider divider_1 (.in_1(A), .in_2(sign), .in_3(B), .out_4(div_res), .out_5(div_rem));
  multiplier multiplier_1 (.in_1(A), .in_2(sign), .in_3(B), .Output(LO), .Output_2(HI));
  Comparator_part #(.width(4)) comparator_2 (.a(Selector), .b(4'b0011), .eq(div));  // open: gt, lt
  Comparator_part #(.width(4)) comparator_3 (.a(Selector), .b(4'b0010), .eq(mult));  // open: gt, lt
  or or_1 (enable, div, mult);
  Multiplexer #(.width(32), .enable("false")) multiplexer_2 (
    .in0(div_res), .in1(LO), .out(multiplexer_2_out), .sel(mult));
  Multiplexer #(.width(32), .enable("false")) multiplexer_3 (
    .in0(div_rem), .in1(HI), .out(multiplexer_3_out), .sel(mult));
  Register #(.width(32)) register_1 (.D(multiplexer_2_out), .en(enable), .Q(Output_2), .clk(in_2));  // open: clr
  Register #(.width(32)) register_2 (.D(multiplexer_3_out), .en(enable), .Q(Output_3), .clk(in_2));  // open: clr

  // Other names for the same wires on the sheet: Clk = in_2; HI_t[31:0] = Output_3; LO_t[31:0] = Output_2;
  //   S[3:0] = Selector

  // Notes on the sheet:
  //   comparator
endmodule

module Comparator (
  input  [31:0] A,
  input  [31:0] B,
  input  sign,
  output [31:0] \output 
);

  wire multiplexer_1_out, slt, sltu;

  Comparator_part #(.width(32), .mode("unsigned")) comparator_1 (.a(A), .b(B), .lt(sltu));  // open: gt, eq
  Comparator_part #(.width(32)) comparator_2 (.a(A), .b(B), .lt(slt));  // open: gt, eq
  Multiplexer #(.enable("false")) multiplexer_1 (.in0(slt), .in1(sltu), .out(multiplexer_1_out), .sel(sign));
  assign \output  = {{31{1'b0}}, multiplexer_1_out};  // Bit_Extender bit_extender_1

  // Other names for the same wires on the sheet: no_sign = sign

  // Notes on the sheet:
  //   unsigned
endmodule

module RegisterFile (
  input  [31:0] Data,
  input  [4:0] Selector_B,
  input  [4:0] Selector_A,
  input  [4:0] Data_Adress,
  input  R_W,
  input  Clk,
  input  Rst,
  input  push,
  input  pop,
  input  enPC,
  output [31:0] Output,
  output [31:0] Ouput,
  output [31:0] Output_2
);

  wire _31, L0, L1, L2, L3, L4, L5, L6, L7, L8, L9, L10, L11, L12, L13, L14, L15, L16, L17, L18, L19, L20,
       L21, L22, L23, L24, L25, L26, L27, L28, L29, L30, L31, not_1_out, not_2_out, or_1_out, or_2_out;
  wire [31:0] adder_1_out, multiplexer_2_out, multiplexer_4_out, R0, R1, R2, R3, R4, R5, R6, R7, R8, R9, R10,
       R11, R12, R13, R14, R15, R16, R17, R18, R19, R20, R21, R22, R23, R24, R25, R26, R27, R28, R29, R30,
       SP, subtractor_1_out;

  Demultiplexer #(.select(5), .enable("false")) demultiplexer_1 (
    .out0(L0), .out1(L1), .out2(L2), .out3(L3), .out4(L4), .out5(L5), .out6(L6), .out7(L7), .out8(L8),
    .out9(L9), .out10(L10), .out11(L11), .out12(L12), .out13(L13), .out14(L14), .out15(L15), .out16(L16),
    .out17(L17), .out18(L18), .out19(L19), .out20(L20), .out21(L21), .out22(L22), .out23(L23), .out24(L24),
    .out25(L25), .out26(L26), .out27(L27), .out28(L28), .out29(L29), .out30(L30), .out31(L31), .in(R_W),
    .sel(Data_Adress));
  Register #(.width(32)) register_1 (.D({32{1'b0}}), .en(L0), .Q(R0), .clk(Clk), .clr(Rst));
  Register #(.width(32)) register_2 (.D(Data), .en(L6), .Q(R6), .clk(Clk), .clr(Rst));
  Register #(.width(32)) register_3 (.D(Data), .en(L12), .Q(R12), .clk(Clk), .clr(Rst));
  Register #(.width(32)) register_4 (.D(Data), .en(L18), .Q(R18), .clk(Clk), .clr(Rst));
  Register #(.width(32)) register_5 (.D(Data), .en(L24), .Q(R24), .clk(Clk), .clr(Rst));
  Register #(.width(32)) register_6 (.D(Data), .en(L30), .Q(R30), .clk(Clk), .clr(Rst));
  Register #(.width(32)) register_7 (.D(Data), .en(L1), .Q(R1), .clk(Clk), .clr(Rst));
  Register #(.width(32)) register_8 (.D(Data), .en(L7), .Q(R7), .clk(Clk), .clr(Rst));
  Register #(.width(32)) register_9 (.D(Data), .en(L13), .Q(R13), .clk(Clk), .clr(Rst));
  Register #(.width(32)) register_10 (.D(Data), .en(L19), .Q(R19), .clk(Clk));  // open: clr
  Register #(.width(32)) register_11 (.D(Data), .en(L25), .Q(R25), .clk(Clk));  // open: clr
  Multiplexer #(.select(5), .width(32)) multiplexer_1 (
    .in0(R0), .in1(R1), .in2(R2), .in3(R3), .in4(R4), .in5(R5), .in6(R6), .in7(R7), .in8(R8), .in9(R9),
    .in10(R10), .in11(R11), .in12(R12), .in13(R13), .in14(R14), .in15(R15), .in16(R16), .in17(R17),
    .in18(R18), .in19(R19), .in20(R20), .in21(R21), .in22(R22), .in23(R23), .in24(R24), .in25(R25),
    .in26(R26), .in27(R27), .in28(R28), .in29(R29), .in30(R30), .in31(Output_2), .out(Output),
    .sel(Selector_A), .en(not_1_out));
  not not_1 (not_1_out, R_W);
  Multiplexer #(.width(32), .enable("false")) multiplexer_2 (.in0(SP), .in1(Data), .out(multiplexer_2_out), .sel(L31));
  Register #(.width(32)) register_12 (.D(Data), .en(L2), .Q(R2), .clk(Clk), .clr(Rst));
  Register #(.width(32)) register_13 (.D(Data), .en(L8), .Q(R8), .clk(Clk));  // open: clr
  Register #(.width(32)) register_14 (.D(Data), .en(L14), .Q(R14), .clk(Clk), .clr(Rst));
  Register #(.width(32)) register_15 (.D(Data), .en(L20), .Q(R20), .clk(Clk), .clr(Rst));
  Register #(.width(32)) register_16 (.D(Data), .en(L26), .Q(R26), .clk(Clk), .clr(Rst));
  Register #(.width(32)) register_17 (.D(multiplexer_2_out), .en(or_1_out), .Q(Output_2), .clk(Clk), .clr(Rst));
  or or_1 (or_1_out, L31, _31, Rst);
  Register #(.width(32)) register_18 (.D(Data), .en(L3), .Q(R3), .clk(Clk), .clr(Rst));
  Register #(.width(32)) register_19 (.D(Data), .en(L9), .Q(R9), .clk(Clk), .clr(Rst));
  Register #(.width(32)) register_20 (.D(Data), .en(L15), .Q(R15), .clk(Clk), .clr(Rst));
  Register #(.width(32)) register_21 (.D(Data), .en(L21), .Q(R21), .clk(Clk), .clr(Rst));
  Register #(.width(32)) register_22 (.D(Data), .en(L27), .Q(R27), .clk(Clk), .clr(Rst));
  Multiplexer #(.select(5), .width(32)) multiplexer_3 (
    .in0(R0), .in1(R1), .in2(R2), .in3(R3), .in4(R4), .in5(R5), .in6(R6), .in7(R7), .in8(R8), .in9(R9),
    .in10(R10), .in11(R11), .in12(R12), .in13(R13), .in14(R14), .in15(R15), .in16(R16), .in17(R17),
    .in18(R18), .in19(R19), .in20(R20), .in21(R21), .in22(R22), .in23(R23), .in24(R24), .in25(R25),
    .in26(R26), .in27(R27), .in28(R28), .in29(R29), .in30(R30), .in31(Output_2), .out(Ouput),
    .sel(Selector_B), .en(not_2_out));
  not not_2 (not_2_out, R_W);
  Register #(.width(32)) register_23 (.D(Data), .en(L4), .Q(R4), .clk(Clk), .clr(Rst));
  Register #(.width(32)) register_24 (.D(Data), .en(L10), .Q(R10), .clk(Clk), .clr(Rst));
  Register #(.width(32)) register_25 (.D(Data), .en(L16), .Q(R16), .clk(Clk));  // open: clr
  Register #(.width(32)) register_26 (.D(Data), .en(L22), .Q(R22), .clk(Clk));  // open: clr
  Register #(.width(32)) register_27 (.D(Data), .en(L28), .Q(R28), .clk(Clk), .clr(Rst));
  or or_2 (or_2_out, pop, push);
  Subtractor #(.width(32)) subtractor_1 (.a(Output_2), .b(32'h4), .out(subtractor_1_out));  // open: bin, bout
  Adder #(.width(32)) adder_1 (.a(32'h4), .b(Output_2), .out(adder_1_out));  // open: cin, cout
  Register #(.width(32)) register_28 (.D(Data), .en(L5), .Q(R5), .clk(Clk), .clr(Rst));
  Register #(.width(32)) register_29 (.D(Data), .en(L11), .Q(R11), .clk(Clk), .clr(Rst));
  Register #(.width(32)) register_30 (.D(Data), .en(L17), .Q(R17), .clk(Clk), .clr(Rst));
  Register #(.width(32)) register_31 (.D(Data), .en(L23), .Q(R23), .clk(Clk), .clr(Rst));
  Register #(.width(32)) register_32 (.D(Data), .en(L29), .Q(R29), .clk(Clk), .clr(Rst));
  and and_1 (_31, enPC, or_2_out);
  // Probe on subtractor_1_out
  // Probe on adder_1_out
  // Probe on multiplexer_4_out
  Multiplexer #(.width(32), .enable("false")) multiplexer_4 (
    .in0(subtractor_1_out), .in1(adder_1_out), .out(multiplexer_4_out), .sel(pop));
  Multiplexer #(.width(32), .enable("false")) multiplexer_5 (
    .in0(multiplexer_4_out), .in1({32{1'b0}}), .out(SP), .sel(Rst));

  // Other names for the same wires on the sheet: A[31:0] = Output; B[31:0] = Ouput; DA[4:0] = Data_Adress;
  //   DI[31:0] = Data; enSP = enPC; R31[31:0] = Output_2; SA[4:0] = Selector_A; SB[4:0] = Selector_B
endmodule

module Register_File_Input (
  input  in_1,
  input  in_2,
  input  in_3,
  input  in_4,
  input  [31:0] in_5,
  input  in_6,
  input  in_7,
  input  in_8,
  input  [31:0] in_9,
  input  [6:0] Kbd_data,
  input  [31:0] in_11,
  input  [31:0] in_12,
  input  [31:0] in_13,
  output [31:0] Output
);

  wire or_1_out;
  wire [2:0] selector;
  wire [31:0] kbd_t;

  or or_1 (or_1_out, in_1, in_6);
  Multiplexer #(.select(3), .width(32), .enable("false")) multiplexer_1 (
    .in0(in_5), .in1(in_11), .in2(in_12), .in3(in_13), .in4(in_9), .in5(kbd_t), .out(Output), .sel(selector));  // open: in6, in7
  Priority_Encoder priority_encoder_1 (
    .in0(1'b1), .in1(or_1_out), .in2(in_2), .in3(in_7), .in4(in_8), .in5(in_3), .out(selector));  // open: in6, in7, en_in, gs, en_out
  // Probe on kbd_t
  Multiplexer #(.width(32), .enable("false")) multiplexer_2 (
    .in0({32{1'b1}}), .in1({{25{1'b0}}, Kbd_data}), .out(kbd_t), .sel(in_4));

  // Other names for the same wires on the sheet: ALU[31:0] = in_5; HI[31:0] = in_12; is_kbd = in_3; is_rnd = in_8;
  //   KBD[6:0] = Kbd_data; Kbd_avaible = in_4; LO[31:0] = in_13; Lw = in_1; M[31:0] = in_11; mfhi = in_2; mflo = in_7;
  //   pop = in_6; Rnd[31:0] = in_9
endmodule

module ControlUnit (
  input  in_1,
  input  in_2,
  input  in_3,
  input  in_4,
  input  in_5,
  input  in_6,
  input  in_7,
  input  in_8,
  input  in_9,
  input  in_10,
  input  in_11,
  input  in_12,
  output Output,
  output Output_2,
  output Output_3,
  output Output_4,
  output Output_5,
  output Output_6,
  output Output_7,
  output Output_8,
  output Output_9
);

  wire branch, d_ff_1_q, d_ff_2_q, d_ff_3_q, d_ff_4_q, demultiplexer_1_out0, demultiplexer_1_out1, or_2_out,
       RF;
  wire [2:0] selector;

  D_Flip_Flop #(.trigger("falling")) d_ff_1 (.clk(in_2), .D(in_1), .Q(d_ff_1_q), .reset(in_3));  // open: Qn, preset, en
  D_Flip_Flop #(.trigger("falling")) d_ff_2 (.clk(in_2), .D(in_6), .Q(d_ff_2_q));  // open: Qn, preset, en, reset
  Demultiplexer #(.select(3), .enable("false")) demultiplexer_1 (
    .out0(demultiplexer_1_out0), .out1(demultiplexer_1_out1), .out2(branch), .out3(Output_5),
    .out4(Output_6), .out5(RF), .in(d_ff_2_q), .sel(selector));  // open: out6, out7
  Priority_Encoder priority_encoder_1 (
    .in0(1'b1), .in1(in_7), .in2(in_8), .in3(in_9), .in4(in_10), .in5(in_11), .out(selector));  // open: in6, in7, en_in, gs, en_out
  // Probe on selector
  or or_1 (Output, d_ff_1_q, d_ff_3_q);
  D_Flip_Flop #(.trigger("falling")) d_ff_3 (
    .clk(in_2), .D(Output_3), .Q(d_ff_3_q), .reset(in_3));  // open: Qn, preset, en
  or or_2 (or_2_out, Output_7, demultiplexer_1_out0);
  D_Flip_Flop #(.trigger("falling")) d_ff_4 (
    .clk(in_2), .D(demultiplexer_1_out1), .Q(d_ff_4_q), .reset(in_3));  // open: Qn, preset, en
  D_Flip_Flop #(.trigger("falling")) d_ff_5 (
    .clk(in_2), .D(or_2_out), .Q(Output_7), .reset(in_3));  // open: Qn, preset, en
  or or_3 (Output_9, in_12, Output_8);
  or or_4 (Output_4, d_ff_4_q, in_5, RF);
  D_Flip_Flop #(.trigger("falling")) d_ff_6 (
    .clk(in_2), .D(Output_4), .Q(Output_8), .reset(in_3));  // open: Qn, preset, en
  or or_5 (Output_3, Output_8, branch, in_4);

  assign Output_2 = in_6;

  // Other names for the same wires on the sheet: ALU_Inst = in_7; clk = in_2; end = Output_7;
  //   get_another_inst = Output_3; PC_en = Output_3; get_Data = Output_5; get_Inst = Output; Jump_Inst = in_8;
  //   read_Mem_Inst = in_9; ready_write = in_4; readyData = in_5; IC_en = in_6; readyInst = in_6; reset = in_3;
  //   RF_en = Output_4; Save_Inst = in_11; start = in_1; kbd_en = Output_8; tty = Output_8; tty_en = Output_9;
  //   tty_Inst = in_12; write = Output_6; write_Mem_Inst = in_10

  // Notes on the sheet:
  //   Output:
endmodule

module ReadRam (
  input  [31:0] in_1,
  input  [31:0] in_2,
  input  [31:0] in_3,
  input  [31:0] in_4,
  input  [3:0] in_5,
  input  in_6,
  input  in_7,
  input  in_8,
  output [31:0] Output,
  output [31:0] Output_2,
  output [31:0] Output_3,
  output [31:0] Output_4,
  output Output_5,
  output Output_6
);

  wire finish_r, or_1_out, start_r, stop;

  // Probe on in_1
  D_Flip_Flop #(.trigger("falling")) d_ff_1 (
    .clk(in_6), .D(in_8), .Q(start_r), .en(or_1_out));  // open: Qn, preset, reset
  or or_1 (or_1_out, in_8, stop);
  Register #(.width(32)) register_1 (.D(in_1), .en(finish_r), .Q(Output), .clk(in_6), .clr(in_7));
  timer timer_1 (.in_1(start_r), .in_2(Output_6), .in_3(in_6), .in_4(in_5), .Output(stop));
  Register #(.width(32)) register_2 (.D(in_2), .en(finish_r), .Q(Output_2), .clk(in_6), .clr(in_7));
  D_Flip_Flop #(.trigger("falling")) d_ff_2 (
    .clk(in_6), .D(stop), .Q(finish_r), .reset(Output_6));  // open: Qn, preset, en
  D_Flip_Flop #(.trigger("falling")) d_ff_3 (.clk(in_6), .D(finish_r), .Q(Output_6));  // open: Qn, preset, en, reset
  Register #(.width(32)) register_3 (.D(in_3), .en(finish_r), .Q(Output_3), .clk(in_6), .clr(in_7));
  or or_2 (Output_5, start_r, finish_r);
  Register #(.width(32)) register_4 (.D(in_4), .en(finish_r), .Q(Output_4), .clk(in_6), .clr(in_7));

  // Other names for the same wires on the sheet: bank_0[31:0] = in_1; bank_1[31:0] = in_2; bank_2[31:0] = in_3;
  //   bank_3[31:0] = in_4; clock = in_6; CS = Output_5; get = in_8; out_bank0[31:0] = Output;
  //   out_bank1[31:0] = Output_2; out_bank2[31:0] = Output_3; out_bank3[31:0] = Output_4; read_time[3:0] = in_5;
  //   ready = Output_6; reset = in_7
endmodule

module timer (
  input  in_1,
  input  in_2,
  input  in_3,
  input  [3:0] in_4,
  output Output
);

  wire [3:0] counter_1_q;

  Counter #(.width(4), .max('hf)) counter_1 (
    .count(in_1), .Q(counter_1_q), .clk(in_3), .clr(in_2));  // open: load, D, carry
  Comparator_part #(.width(4)) comparator_1 (.a(in_4), .b(counter_1_q), .eq(Output));  // open: gt, lt

  // Other names for the same wires on the sheet: clock = in_3; ready = Output; reset = in_2; start = in_1;
  //   wait_time[3:0] = in_4
endmodule

module RamInteraction (
  input  [31:0] in_1,
  input  [31:0] in_2,
  input  [31:0] in_3,
  input  [31:0] in_4,
  input  [31:0] in_5,
  input  [3:0] in_6,
  input  [3:0] in_7,
  input  in_8,
  input  in_9,
  input  in_10,
  input  in_11,
  input  in_12,
  input  in_13,
  output [31:0] Output,
  output [31:0] Output_2,
  output [31:0] Output_3,
  output [31:0] Output_4,
  output [15:0] Output_5,
  output [3:0] Output_6,
  output Output_7,
  output Output_8,
  output Output_9,
  output Output_10,
  output Output_11
);

  wire CSD, CSI, or_1_out, stop;
  wire [31:0] D0, D1, D2, D3, I0, I1, I2, I3, swapbits_1_output, swapbits_2_output, swapbits_3_output,
       swapbits_4_output;

  SwapBits swapbits_1 (.in_1(D0), .Output(swapbits_1_output));
  Multiplexer #(.width(32), .enable("false")) multiplexer_1 (
    .in0(swapbits_1_output), .in1(I0), .out(Output), .sel(in_13));
  D_Flip_Flop #(.trigger("falling")) d_ff_1 (
    .clk(in_8), .D(in_11), .Q(Output_7), .en(or_1_out));  // open: Qn, preset, reset
  or or_1 (or_1_out, in_11, stop);
  SwapBits swapbits_2 (.in_1(D1), .Output(swapbits_2_output));
  Demultiplexer #(.select(2), .enable("false")) demultiplexer_1 (
    .out0(Output_6[0]), .out1(Output_6[1]), .out2(Output_6[2]), .out3(Output_6[3]), .in(1'b1), .sel(in_5[3:2]));
  Multiplexer #(.width(32), .enable("false")) multiplexer_2 (
    .in0(swapbits_2_output), .in1(I1), .out(Output_2), .sel(in_13));
  timer timer_1 (.in_1(Output_7), .in_2(Output_11), .in_3(in_8), .in_4(in_7), .Output(stop));
  SwapBits swapbits_3 (.in_1(D2), .Output(swapbits_3_output));
  ReadRam readram_1 (
    .in_1(in_1), .in_2(in_2), .in_3(in_3), .in_4(in_4), .in_5(in_6), .in_6(in_8), .in_7(in_9), .in_8(in_10),
    .Output(I0), .Output_2(I1), .Output_3(I2), .Output_4(I3), .Output_5(CSI), .Output_6(Output_9));
  ReadRam readram_2 (
    .in_1(in_1), .in_2(in_2), .in_3(in_3), .in_4(in_4), .in_5(in_6), .in_6(in_8), .in_7(in_9), .in_8(in_12),
    .Output(D0), .Output_2(D1), .Output_3(D2), .Output_4(D3), .Output_5(CSD), .Output_6(Output_10));
  Multiplexer #(.width(32), .enable("false")) multiplexer_3 (
    .in0(swapbits_3_output), .in1(I2), .out(Output_3), .sel(in_13));
  D_Flip_Flop #(.trigger("falling")) d_ff_2 (.clk(in_8), .D(stop), .Q(Output_11));  // open: Qn, preset, en, reset
  // Probe on I3
  or or_2 (Output_8, CSD, CSI, Output_7);
  SwapBits swapbits_4 (.in_1(D3), .Output(swapbits_4_output));
  // Probe on I3
  Multiplexer #(.width(32), .enable("false")) multiplexer_4 (
    .in0(swapbits_4_output), .in1(I3), .out(Output_4), .sel(in_13));
  // Probe on Output_4

  assign Output_5 = in_5[19:4];

  // Other names for the same wires on the sheet: bank0[31:0] = in_1; bank1[31:0] = in_2; bank2[31:0] = in_3;
  //   bank3[31:0] = in_4; clock = in_8; CS = Output_8; get_data = in_12; get_inst = in_10; isInstruction = in_13;
  //   mask[3:0] = Output_6; out_bank0[31:0] = Output; out_bank1[31:0] = Output_2; out_bank2[31:0] = Output_3;
  //   out_bank3[31:0] = Output_4; R_W = Output_7; Ram_Address[31:0] = in_5; address[15:0] = in_5[19:4];
  //   read_time[3:0] = in_6; Ready_data = Output_10; Ready_inst = Output_9; ready_write = Output_11; reset = in_9;
  //   write = in_11; write_time[3:0] = in_7

  // Notes on the sheet:
  //   Write:
  //   Read Instruction:
  //   Read Data:
endmodule

module MemoryAddress (
  input  [31:0] in_1,
  input  [31:0] in_2,
  input  [31:0] in_3,
  input  in_4,
  input  in_5,
  input  in_6,
  input  in_7,
  input  in_8,
  output [31:0] Output
);

  wire [1:0] or_2_out;
  wire [31:0] multiplexer_1_out, subtractor_1_out;

  Multiplexer #(.width(32), .enable("false")) multiplexer_1 (
    .in0(in_3), .in1(subtractor_1_out), .out(multiplexer_1_out), .sel(in_7));
  Subtractor #(.width(32)) subtractor_1 (.a(in_3), .b(32'h4), .out(subtractor_1_out));  // open: bin, bout
  or or_1 (or_2_out[1], in_6, in_8, in_7);
  Multiplexer #(.select(2), .width(32), .enable("false")) multiplexer_2 (
    .in0(in_1), .in1(in_2), .in2(multiplexer_1_out), .in3(in_1), .out(Output), .sel(or_2_out));
  or or_2 (or_2_out[0], in_4, in_8, in_5);

  // Other names for the same wires on the sheet: ALU[31:0] = in_2; isPC = in_8; lw = in_4; PC[31:0] = in_1;
  //   pop = in_6; push = in_7; SP[31:0] = in_3; sw = in_5
endmodule

module SwapBits (
  input  [31:0] in_1,
  output [31:0] Output
);


  assign Output = {in_1[7:0], in_1[15:8], in_1[23:16], in_1[31:24]};
endmodule

module divider (
  input  [31:0] in_1,
  input  in_2,
  input  [31:0] in_3,
  output [31:0] out_4,
  output [31:0] out_5
);

  wire neg_a, neg_b, neg_div, not_1_out;
  wire [31:0] abs_a, abs_b, abs_div, adder_1_out, divider_1_out, multiplexer_3_out, negator_1_out,
       negator_2_out, negator_3_out, negator_4_out, res, subtractor_1_out;

  not not_1 (not_1_out, in_2);
  Negator #(.width(32)) negator_1 (.in(in_1), .out(negator_1_out));
  Negator #(.width(32)) negator_2 (.in(in_3), .out(negator_2_out));
  and and_1 (neg_a, in_1[31], not_1_out);
  and and_2 (neg_b, not_1_out, in_3[31]);
  Multiplexer #(.width(32), .enable("false")) multiplexer_1 (.in0(in_1), .in1(negator_1_out), .out(abs_a), .sel(neg_a));
  Multiplexer #(.width(32), .enable("false")) multiplexer_2 (.in0(in_3), .in1(negator_2_out), .out(abs_b), .sel(neg_b));
  xor xor_1 (neg_div, neg_a, neg_b);
  Divider #(.width(32)) divider_1 (.a(abs_a), .b(abs_b), .out(divider_1_out), .rem(res));  // open: upper
  Adder #(.width(32)) adder_1 (.a(divider_1_out), .b(32'h1), .out(adder_1_out));  // open: cin, cout
  Multiplexer #(.width(32), .enable("false")) multiplexer_3 (
    .in0(divider_1_out), .in1(adder_1_out), .out(multiplexer_3_out), .sel(neg_a));
  Subtractor #(.width(32)) subtractor_1 (.a(abs_b), .b(res), .out(subtractor_1_out));  // open: bin, bout
  Negator #(.width(32)) negator_3 (.in(abs_div), .out(negator_3_out));
  Negator #(.width(32)) negator_4 (.in(multiplexer_3_out), .out(negator_4_out));
  Multiplexer #(.width(32), .enable("false")) multiplexer_4 (
    .in0(res), .in1(subtractor_1_out), .out(out_5), .sel(neg_a));
  Multiplexer #(.width(32), .enable("false")) multiplexer_5 (
    .in0(abs_div), .in1(negator_3_out), .out(out_4), .sel(neg_div));
  Multiplexer #(.width(32), .enable("false")) multiplexer_6 (
    .in0(multiplexer_3_out), .in1(negator_4_out), .out(abs_div), .sel(neg_div));

  // Other names for the same wires on the sheet: a[31:0] = in_1; b[31:0] = in_3; div[31:0] = out_4; no_sign = in_2;
  //   remainder[31:0] = out_5
endmodule

module multiplier (
  input  [31:0] in_1,
  input  in_2,
  input  [31:0] in_3,
  output [31:0] Output,
  output [31:0] Output_2
);

  wire [31:0] Hi, HiU, Lo, LoU, multiplexer_1_out, multiplexer_2_out, no_a, no_b, not_1_out, not_2_out;

  // Probe on in_1
  assign not_1_out = ~in_1;  // NOT_Gate not_1, 32 bits wide
  Adder #(.width(32)) adder_1 (.a(not_1_out), .b(32'h1), .out(no_a));  // open: cin, cout
  assign not_2_out = ~in_3;  // NOT_Gate not_2, 32 bits wide
  Adder #(.width(32)) adder_2 (.a(not_2_out), .b(32'h1), .out(no_b));  // open: cin, cout
  // Probe on in_3
  Multiplexer #(.width(32), .enable("false")) multiplexer_1 (
    .in0(in_1), .in1(no_a), .out(multiplexer_1_out), .sel(in_1[31]));
  Multiplexer #(.width(32), .enable("false")) multiplexer_2 (
    .in0(in_3), .in1(no_b), .out(multiplexer_2_out), .sel(in_3[31]));
  Multiplier #(.width(32)) multiplier_1 (.a(in_1), .b(in_3), .out(Lo), .cout(Hi));  // open: cin
  Multiplier #(.width(32)) multiplier_2 (
    .a(multiplexer_1_out), .b(multiplexer_2_out), .out(LoU), .cout(HiU));  // open: cin
  Multiplexer #(.width(32), .enable("false")) multiplexer_3 (.in0(Lo), .in1(LoU), .out(Output), .sel(in_2));
  Multiplexer #(.width(32), .enable("false")) multiplexer_4 (.in0(Hi), .in1(HiU), .out(Output_2), .sel(in_2));
  // Probe on Output

  // Other names for the same wires on the sheet: a[31:0] = in_1; sign_a = in_1[31]; b[31:0] = in_3; sign_b = in_3[31];
  //   sign = in_2
endmodule
